# Fritzing sketch 3gAlarmPanel-UI (saved by Fritzing 0.9.3b)
breadboards: 1

parts:
  R7 = Resistor [tolerance=±5% resistance=220k package=THT]
  R5 = Resistor [tolerance=±5% resistance=220 package=THT]
  Part1 = Arduino Uno (Rev3)
  R3 = Resistor [tolerance=±5% resistance=220 package=THT]
  Part2 = Adafruit FONA 808 Breakout [part_number="Adafruit #2542"]
  R6 = Resistor [tolerance=±5% resistance=220k package=THT]
  R1 = Resistor [tolerance=±5% resistance=220 package=THT]
  R8 = Resistor [tolerance=±5% resistance=220k package=THT]
  LED2 = RGB LED (com. cathode, rgb) [package="5 mm [THT]"]
  R2 = Resistor [tolerance=±5% resistance=220 package=THT]
  R4 = Resistor [tolerance=±5% resistance=220 package=THT]
  DHT1 = DHT11 Humitidy and Temperature Sensor
  J2 = female pin header, 2 pins [form="♀ (female)"]

nets:
  LED_GREEN: R7.Pin_0, Part1.D9_PWM
  N1: R7.Pin_1, LED2.green_anode
  VOLTAGE0: R5.Pin_0, Part1.A0, R4.Pin_0
  GND: R5.Pin_1, Part1.GND, R3.Pin_1, Part2.GND, LED2.common_cathode, DHT1.GND
  VOLTAGE1: Part1.A1, R3.Pin_0, R2.Pin_0
  LED_RED: Part1.D8, R6.Pin_0
  LED_BLUE: Part1.D10_PWM/SS, R8.Pin_0
  FONA_RXD: Part1.D2, Part2.RXD
  FONA_TXD: Part1.D3_PWM, Part2.TXD
  DHT11_DATA: Part1.D5_PWM, R1.Pin_1, DHT1.DATA
  FONA_RESET: Part1.D6_PWM, Part2.Reset
  FONA_POWER: Part1.D7, Part2.Key
  5V: Part1.5V, Part2.+5V, R1.Pin_0, DHT1.VDD
  N2: R6.Pin_1, LED2.red_anode
  N3: R8.Pin_1, LED2.blue_anode
  N4: R2.Pin_1, J2.pin2
  N5: R4.Pin_1, J2.pin1

custom parts:
  Adafruit FONA 808 Breakout: Cellular + GPS tracking, all in one? Oh yes! Introducing Adafruit FONA 808 MiniGSM + GPS, an all-in-one cellular phone module with that lets you add location-tracking, voice, text, SMS and data to your project in an adorable little package.
  DHT11 Humitidy and Temperature Sensor: DHT11 Humidity and Temperature Sensor
